# Fritzing sketch PedestrianTrafficLight (saved by Fritzing 0.8.3b)
breadboards: 2

parts:
  Part1 = Arduino Leonardo (Rev3b)
  LED2 = LED - 5mm [color="Green (560nm)" package="5 mm [THT]"]
  LED3 = LED - 5mm [color="Red (633nm)" package="5 mm [THT]"]
  LED4 = LED - 5mm [color="Yellow (585nm)" package="5 mm [THT]"]
  LED5 = LED - 5mm [color="Green (560nm)" package="5 mm [THT]"]
  R1 = Resistor [tolerance=±5% resistance=1k package=THT]
  R2 = Resistor [tolerance=±5% resistance=1k package=THT]
  R3 = Resistor [tolerance=±5% resistance=1k package=THT]
  R4 = Resistor [tolerance=±5% resistance=1k package=THT]
  R5 = Resistor [tolerance=±5% resistance=1k package=THT]
  LED6 = LED - 5mm [color="Red (633nm)" package="5 mm [THT]"]

nets:
  N1: Part1.D1/TX, R3.Pin_1
  N2: Part1.D2/SDA, R4.Pin_1
  N3: Part1.D3_PWM/SCL, R5.Pin_1
  N4: Part1.D4/A6, R1.Pin_0
  N5: Part1.D5_PWM, R2.Pin_0
  N6: Part1.GND, LED2.cathode, LED3.cathode, LED4.cathode, LED5.cathode, LED6.cathode
  N7: LED2.anode, R2.Pin_1
  N8: LED3.anode, R3.Pin_0
  N9: LED4.anode, R4.Pin_0
  N10: LED5.anode, R5.Pin_0
  N11: R1.Pin_1, LED6.anode

notes:
  Pedestrian Traffic Light, http://github.com/cniesen/ArduinoPedestrianTrafficLight, 1.0
  Pedestrian Light
  Traffic Light
